// Logisim project 111.circ as structural Verilog: 1 circuit, main circuit main
module main (
  input  [7:0] in_1,
  input  in_2,
  input  [7:0] in_3,
  input  in_4,
  input  [7:0] in_5,
  input  in_6
);

  wire clk, demultiplexer_1_out0, demultiplexer_1_out1, demultiplexer_1_out2, demultiplexer_1_out3,
       demultiplexer_1_out4, demultiplexer_1_out5, demultiplexer_1_out6, demultiplexer_1_out7,
       demultiplexer_1_out8, demultiplexer_1_out9, demultiplexer_1_out10, demultiplexer_1_out11,
       demultiplexer_1_out12, demultiplexer_1_out13, demultiplexer_1_out14, demultiplexer_1_out15;
  wire [7:0] register_1_q, register_2_q, register_3_q;
  wire [15:0] register_4_q, register_5_q, register_6_q, register_7_q, register_8_q, register_9_q,
       register_10_q, register_11_q, register_12_q, register_13_q, register_14_q, register_15_q,
       register_16_q, register_17_q, register_18_q, register_19_q;

  Clock clock_1 (.out(clk));
  Register register_1 (.D(in_1), .en(in_2), .Q(register_1_q), .clr(clk));  // open: clk
  Register register_2 (.D(in_3), .en(in_4), .Q(register_2_q), .clr(clk));  // open: clk
  Demultiplexer #(.select(4)) demultiplexer_1 (
    .out0(demultiplexer_1_out0), .out1(demultiplexer_1_out1), .out2(demultiplexer_1_out2),
    .out3(demultiplexer_1_out3), .out4(demultiplexer_1_out4), .out5(demultiplexer_1_out5),
    .out6(demultiplexer_1_out6), .out7(demultiplexer_1_out7), .out8(demultiplexer_1_out8),
    .out9(demultiplexer_1_out9), .out10(demultiplexer_1_out10), .out11(demultiplexer_1_out11),
    .out12(demultiplexer_1_out12), .out13(demultiplexer_1_out13), .out14(demultiplexer_1_out14),
    .out15(demultiplexer_1_out15), .in(in_6), .sel(register_3_q[3:0]), .en(in_6));
  Register register_3 (.D(in_5), .en(in_6), .Q(register_3_q), .clr(clk));  // open: clk
  // Probe on register_3_q
  Register #(.width(16)) register_4 (
    .D({register_2_q, register_1_q}), .en(demultiplexer_1_out0), .Q(register_4_q), .clk(clk));  // open: clr
  Register #(.width(16)) register_5 (
    .D({register_2_q, register_1_q}), .en(demultiplexer_1_out1), .Q(register_5_q), .clk(clk));  // open: clr
  Register #(.width(16)) register_6 (
    .D({register_2_q, register_1_q}), .en(demultiplexer_1_out2), .Q(register_6_q), .clk(clk));  // open: clr
  Register #(.width(16)) register_7 (
    .D({register_2_q, register_1_q}), .en(demultiplexer_1_out3), .Q(register_7_q), .clk(clk));  // open: clr
  Register #(.width(16)) register_8 (
    .D({register_2_q, register_1_q}), .en(demultiplexer_1_out4), .Q(register_8_q), .clk(clk));  // open: clr
  Register #(.width(16)) register_9 (
    .D({register_2_q, register_1_q}), .en(demultiplexer_1_out5), .Q(register_9_q), .clk(clk));  // open: clr
  Register #(.width(16)) register_10 (
    .D({register_2_q, register_1_q}), .en(demultiplexer_1_out6), .Q(register_10_q), .clk(clk));  // open: clr
  Register #(.width(16)) register_11 (
    .D({register_2_q, register_1_q}), .en(demultiplexer_1_out7), .Q(register_11_q), .clk(clk));  // open: clr
  Register #(.width(16)) register_12 (
    .D({register_2_q, register_1_q}), .en(demultiplexer_1_out8), .Q(register_12_q), .clk(clk));  // open: clr
  Register #(.width(16)) register_13 (
    .D({register_2_q, register_1_q}), .en(demultiplexer_1_out9), .Q(register_13_q), .clk(clk));  // open: clr
  Register #(.width(16)) register_14 (
    .D({register_2_q, register_1_q}), .en(demultiplexer_1_out10), .Q(register_14_q), .clk(clk));  // open: clr
  Register #(.width(16)) register_15 (
    .D({register_2_q, register_1_q}), .en(demultiplexer_1_out11), .Q(register_15_q), .clk(clk));  // open: clr
  Register #(.width(16)) register_16 (
    .D({register_2_q, register_1_q}), .en(demultiplexer_1_out12), .Q(register_16_q), .clk(clk));  // open: clr
  Register #(.width(16)) register_17 (
    .D({register_2_q, register_1_q}), .en(demultiplexer_1_out13), .Q(register_17_q), .clk(clk));  // open: clr
  Register #(.width(16)) register_18 (
    .D({register_2_q, register_1_q}), .en(demultiplexer_1_out14), .Q(register_18_q), .clk(clk));  // open: clr
  Register #(.width(16)) register_19 (
    .D({register_2_q, register_1_q}), .en(demultiplexer_1_out15), .Q(register_19_q), .clk(clk));  // open: clr
  DotMatrix #(.inputtype("row"), .matrixcols(16), .matrixrows(16), .dotshape("circle")) dotmatrix_1 (
    .row0(register_4_q), .row1(register_5_q), .row2(register_6_q), .row3(register_7_q), .row4(register_8_q),
    .row5(register_9_q), .row6(register_10_q), .row7(register_11_q), .row8(register_12_q),
    .row9(register_13_q), .row10(register_14_q), .row11(register_15_q), .row12(register_16_q),
    .row13(register_17_q), .row14(register_18_q), .row15(register_19_q));

  // Notes on the sheet:
  //   sel
  //   lo
  //   hi
  //   selector
endmodule
